# Fritzing sketch Diagram (saved by Fritzing 1.0.6)
breadboards: 1

parts:
  Elegoo_Arduino_Uno_R3 = Arduino Uno (Rev3) - ICSP
  L298N_Motor_Driver = L298 [package=multiwatt15]
  NEMA_17_Stepper_Motor = Stepper Motor - Bipolar
  HC-05_Bluetooth = Bluetooth HC-05 Macho

nets:
  N1: Elegoo_Arduino_Uno_R3.ICSP_MOSI, Elegoo_Arduino_Uno_R3.D11_PWM/MOSI, HC-05_Bluetooth.RXD
  GND: Elegoo_Arduino_Uno_R3.GND, L298N_Motor_Driver.GND, HC-05_Bluetooth.GND
  5V: Elegoo_Arduino_Uno_R3.5V, HC-05_Bluetooth.VCC
  N2: Elegoo_Arduino_Uno_R3.D9_PWM, HC-05_Bluetooth.State
  N3: Elegoo_Arduino_Uno_R3.D10_PWM/SS, HC-05_Bluetooth.TXD
  N4: Elegoo_Arduino_Uno_R3.D3_PWM, L298N_Motor_Driver.IN1
  N5: Elegoo_Arduino_Uno_R3.D4, L298N_Motor_Driver.IN2
  N6: Elegoo_Arduino_Uno_R3.D5_PWM, L298N_Motor_Driver.IN3
  N7: Elegoo_Arduino_Uno_R3.D6_PWM, L298N_Motor_Driver.IN4
  9V: Elegoo_Arduino_Uno_R3.VIN, L298N_Motor_Driver.VS
  N8: L298N_Motor_Driver.OUT1, NEMA_17_Stepper_Motor.A
  N9: L298N_Motor_Driver.OUT2, NEMA_17_Stepper_Motor.B
  N10: L298N_Motor_Driver.OUT3, NEMA_17_Stepper_Motor.C
  N11: L298N_Motor_Driver.OUT4, NEMA_17_Stepper_Motor.D
